# Fritzing sketch soil moisture (saved by Fritzing 0.9.3b)
breadboards: 2

parts:
  U1 = NodeMCU V1.0
  Part1 = Soil Moisture Sensor
  U4 = RELAY [package=relay-t9a]
  BAT1 = Battery Holders [package=lipo-1100mAh]
  BAT2 = Battery Holders [package=lipo-1100mAh]  # not connected
  BAT3 = Battery Holders [package=lipo-1100mAh]
  M1 = DC Motor
  RHT1 = Humidity and Temperature Sensor RHT03
  IC1 = Voltage Regulator [package=to-220-alt]
  D1 = Diode [package=diode-hv]
  U5 = SWITCH-SPST-2 [package=r_sw_th]

nets:
  N1: U1.D1, U4.COIL1
  N2: U1.D3, RHT1.Data-signal
  GND: U1.GND, Part1.GND, U4.MAIN, BAT3.-, M1.pin_2, RHT1.GND_2, IC1.GND
  VCC: U1.Vin, Part1.VCC, U4.COIL2, RHT1.Vcc, IC1.OUT
  N3: U1.A0, Part1.SIG
  N4: U4.NC, M1.pin_1
  N5: U4.NO, BAT1.+, U5.O
  N6: IC1.IN, D1.C
  N7: D1.A, U5.P

custom parts:
  NodeMCU V1.0: ESP9266 based NodeMCU
